# Fritzing sketch SCARA PCB (saved by Fritzing 0.9.0b)
circuit board: 11.4416cm x 12.998cm
breadboards: 2

parts:
  Part2 = Arduino Uno (Rev3)
  741 = DIP - 8 pins [chip_label=741 package="DIP (Dual Inline) [THT]"]
  MAX2 = DIP - 8 pins [chip_label=MAX485 package="DIP (Dual Inline) [THT]"]
  Q2 = NPN-Transistor [package="TO92 [THT]"]
  R7 = Resistor [tolerance=±5% resistance=220 package=THT]
  R8 = Resistor [tolerance=±5% resistance=220 package=THT]
  R9 = Resistor [tolerance=±5% resistance=220 package=THT]
  R10 = Resistor [tolerance=±5% resistance=220 package=THT]
  LED2 = LED - 5mm [color="Red (633nm)" package="5 mm [THT]"]
  R11 = Resistor [tolerance=±5% resistance=220 package=THT]
  R12 = Resistor [tolerance=±5% resistance=220 package=THT]
  J5 = female pin header, 2 pins [form="♀ (female)"]
  J6 = female pin header, 2 pins [form="♀ (female)"]
  J7 = female pin header, 2 pins [form="♀ (female)"]
  C3 = Electrolytic Capacitor [capacitance=1µF package="100 mil [THT, electrolytic]"]
  Power_plug2 = Power plug
  J8 = female pin header, 2 pins [form="♀ (female)"]
  J9 = female pin header, 2 pins [form="♀ (female)"]
  J10 = female pin header, 2 pins [form="♀ (female)"]  # not connected
  J11 = female pin header, 2 pins [form="♀ (female)"]
  J12 = female pin header, 2 pins [form="♀ (female)"]
  J13 = female pin header, 2 pins [form="♀ (female)"]
  J14 = female pin header, 2 pins [form="♀ (female)"]
  J15 = female pin header, 2 pins [form="♀ (female)"]
  J16 = female pin header, 2 pins [form="♀ (female)"]
  J17 = female pin header, 2 pins [form="♀ (female)"]

nets:
  N1: Part2.D13/SCK, R10.Pin_0
  GND: Part2.GND, 741.pin4, MAX2.pin5, Q2.C, R8.Pin_1, R11.Pin_0, J6.pin1, C3.-, Power_plug2.GND, J11.pin2
  N2: Part2.D0/RX, J8.pin2, J13.pin2
  N3: Part2.D1/TX, J8.pin1, J13.pin1
  N4: Part2.5V, 741.pin7, MAX2.pin8, R7.Pin_0, R9.Pin_1, R12.Pin_1
  N5: 741.pin2, R7.Pin_1, R8.Pin_0
  N6: 741.pin3, MAX2.pin2, MAX2.pin3, Q2.E, R9.Pin_0, J16.pin1, J16.pin2
  N7: 741.pin6, LED2.cathode
  N8: MAX2.pin1, R12.Pin_0, J9.pin1, J14.pin2
  N9: MAX2.pin4, J5.pin2, J14.pin1
  N10: MAX2.pin6, J7.pin2
  N11: MAX2.pin7, J7.pin1
  N12: Q2.B, R10.Pin_1
  N13: LED2.anode, R11.Pin_1
  N14: J6.pin2, C3.+, Power_plug2.VCC
  N15: J12.pin1, J12.pin2
  N16: J15.pin1, J17.pin2
  N17: J15.pin2, J17.pin1

custom parts:
  DIP - 8 pins: A DIP stand-in part for whatever IC you want. With 8 pins on a 300mil dual inline package (DIP) footprint.
  DIP - 8 pins: A DIP stand-in part for whatever IC you want. With 8 pins on a 300mil dual inline package (DIP) footprint.
