# Fritzing sketch dynamixel (saved by Fritzing 0.9.0b)
circuit board: 13.9054cm x 9.35395cm
breadboards: 2

parts:
  Part2 = Arduino Uno (Rev3)
  Power_plug2 = Power plug
  C4 = Electrolytic Capacitor [capacitance=1µF package="100 mil [THT, electrolytic]"]
  Q2 = NPN-Transistor [package="TO92 [THT]"]
  R5 = Resistor [tolerance=±5% resistance=220 package=THT]
  LED2 = LED - 5mm [color="Red (633nm)" package="5 mm [THT]"]
  R6 = Resistor [tolerance=±5% resistance=220 package=THT]
  R7 = Resistor [tolerance=±5% resistance=220 package=THT]
  U5 = MAX485 [package=dil08]
  R8 = Resistor [tolerance=±5% resistance=220 package=THT]
  U6 = PIC-ICSP [package=molex-1x6]
  U7 = PIC-ICSP [package=molex-1x6]
  U8 = PIC-ICSP [package=molex-1x6]
  C5 = Electrolytic Capacitor [capacitance=1µF package="100 mil [THT, electrolytic]"]

nets (from the breadboard view):
  N1: Part2.D13/SCK, R6.Pin_1
  GND: Part2.GND, Power_plug2.GND, C4.-, Q2.C, R7.Pin_0, U5.GND, U6.PGC, U8.PGM, C5.+
  5V: Part2.5V, R5.Pin_0, U5.VCC, R8.Pin_0, C5.-
  N2: Power_plug2.VCC, C4.+, U8.PGC
  N3: Q2.E, R5.Pin_1, LED2.anode, U5.RE, U5.DE
  N4: Q2.B, R6.Pin_0
  N5: LED2.cathode, R7.Pin_1
  N6: U5.RO, R8.Pin_1, U7.VCC
  N7: U5.DI, U7.VPP
  N8: U5.A, U8.GND
  N9: U5.B, U8.PGD
