# Fritzing sketch Untitled Sketch (saved by Fritzing 0.9.0b)
circuit board: 15.3662cm x 10.4684cm
breadboards: 2

parts:
  741 = DIP - 8 pins [chip_label=741 package="DIP (Dual Inline) [THT]"]
  MAX1 = DIP - 8 pins [chip_label=MAX485 package="DIP (Dual Inline) [THT]"]
  Q1 = NPN-Transistor [package="TO92 [THT]"]
  R1 = Resistor [tolerance=±5% resistance=220 package=THT]
  R2 = Resistor [tolerance=±5% resistance=220 package=THT]
  R3 = Resistor [tolerance=±5% resistance=220 package=THT]
  R4 = Resistor [tolerance=±5% resistance=220 package=THT]
  LED1 = LED - 5mm [color="Red (633nm)" package="5 mm [THT]"]
  R5 = Resistor [tolerance=±5% resistance=220 package=THT]
  R6 = Resistor [tolerance=±5% resistance=220 package=THT]
  Part1 = Arduino Uno (Rev3)
  J1 = female pin header, 2 pins [form="♀ (female)"]
  J3 = female pin header, 2 pins [form="♀ (female)"]
  J4 = female pin header, 2 pins [form="♀ (female)"]
  C1 = Electrolytic Capacitor [capacitance=1µF package="100 mil [THT, electrolytic]"]
  C2 = Ceramic Capacitor [capacitance=100nF package="100 mil [THT, multilayer]"]
  Power_plug1 = Power plug

nets:
  N1: 741.pin2, R1.Pin_1, R2.Pin_0
  N2: 741.pin3, MAX1.pin2, MAX1.pin3, Q1.E, R3.Pin_0
  GND: 741.pin4, 741.pin7, MAX1.pin5, MAX1.pin8, Q1.C, R1.Pin_0, R2.Pin_1, R3.Pin_1, R5.Pin_0, R6.Pin_1, Part1.GND, J3.pin2, C1.-, C2.0, C2.1, Power_plug1.GND
  N3: 741.pin6, LED1.cathode
  N4: MAX1.pin1, R6.Pin_0, J1.pin1
  N5: MAX1.pin4, J1.pin2
  N6: MAX1.pin6, J4.pin2
  N7: MAX1.pin7, J4.pin1
  N8: Q1.B, R4.Pin_1
  N9: R4.Pin_0, Part1.D13/SCK
  N10: LED1.anode, R5.Pin_1
  N11: J3.pin1, C1.+, Power_plug1.VCC

custom parts:
  DIP - 8 pins: A DIP stand-in part for whatever IC you want. With 8 pins on a 300mil dual inline package (DIP) footprint.
  DIP - 8 pins: A DIP stand-in part for whatever IC you want. With 8 pins on a 300mil dual inline package (DIP) footprint.
