# Fritzing sketch SCARA (saved by Fritzing 0.9.0b)
circuit board: 11.2052cm x 8.77326cm
breadboards: 1

parts:
  U2 = MAX485 [package=dil08]
  R3 = Resistor [tolerance=±5% resistance=220 package=THT]
  CUP_TXD1 = female pin header, 2 pins [form="♀ (female)"]
  dynamixel1 = female pin header, 2 pins [form="♀ (female)"]
  J4 = female pin header, 2 pins [form="♀ (female)"]
  12V1 = Power plug
  Q3 = NPN-Transistor [package="TO92 [THT]"]
  C2 = Electrolytic Capacitor [capacitance=1µF package="100 mil [THT, electrolytic]"]
  R4 = Resistor [tolerance=±5% resistance=220 package=THT]
  J5 = female pin header, 2 pins [form="♀ (female)"]
  J7 = female pin header, 2 pins [form="♀ (female)"]
  J10 = female pin header, 2 pins [form="♀ (female)"]
  J11 = female pin header, 2 pins [form="♀ (female)"]
  J12 = female pin header, 2 pins [form="♀ (female)"]
  J13 = female pin header, 2 pins [form="♀ (female)"]
  J14 = female pin header, 2 pins [form="♀ (female)"]
  J15 = female pin header, 2 pins [form="♀ (female)"]
  J16 = female pin header, 2 pins [form="♀ (female)"]
  J17 = female pin header, 2 pins [form="♀ (female)"]
  J18 = female pin header, 2 pins [form="♀ (female)"]
  J19 = female pin header, 2 pins [form="♀ (female)"]
  J20 = female pin header, 2 pins [form="♀ (female)"]
  J21 = female pin header, 2 pins [form="♀ (female)"]
  J22 = female pin header, 2 pins [form="♀ (female)"]
  R5 = Resistor [tolerance=±5% resistance=220 package=THT]
  Part1 = Arduino Uno (Rev3)
  J6 = female pin header, 2 pins [form="♀ (female)"]
  J23 = female pin header, 2 pins [form="♀ (female)"]
  R6 = Resistor [tolerance=±5% resistance=220 package=THT]
  LED1 = LED - 5mm [color="Red (633nm)" package="5 mm [THT]"]
  J24 = female pin header, 2 pins [form="♀ (female)"]  # not connected
  J25 = female pin header, 2 pins [form="♀ (female)"]  # not connected

nets:
  N1: U2.RO, R3.Pin_0, CUP_TXD1.pin2
  N2: U2.RE, U2.DE, Q3.C, R4.Pin_0, LED1.cathode
  N3: U2.DI, CUP_TXD1.pin1
  N4: U2.GND, Q3.E
  N5: U2.A, dynamixel1.pin2
  N6: U2.B, dynamixel1.pin1
  VCC: U2.VCC, R3.Pin_1, R4.Pin_1, J22.pin2, Part1.5V, R6.Pin_1
  N7: J4.pin1, 12V1.VCC, C2.+
  GND: J4.pin2, 12V1.GND, C2.-, J5.pin1, J7.pin1, J22.pin1, Part1.GND, J23.pin2
  N8: Q3.B, R5.Pin_1
  N9: J7.pin2, Part1.AREF
  N10: J10.pin1, Part1.D12/MISO
  N11: J10.pin2, R5.Pin_0, Part1.D13/SCK
  N12: J11.pin1, Part1.D10_PWM/SS
  N13: J11.pin2, Part1.D11_PWM/MOSI
  N14: J12.pin1, Part1.D8
  N15: J12.pin2, Part1.D9_PWM
  N16: J13.pin1, Part1.D6_PWM
  N17: J13.pin2, Part1.D7
  N18: J14.pin1, Part1.D4
  N19: J14.pin2, Part1.D5_PWM
  N20: J15.pin1, Part1.D2
  N21: J15.pin2, Part1.D3_PWM
  N22: J16.pin1, J16.pin2, Part1.D0/RX, Part1.D1/TX
  N23: J17.pin1, Part1.A5/SCL, J6.pin2
  N24: J17.pin2, Part1.A4/SDA, J6.pin1
  N25: J18.pin1, Part1.A1
  N26: J18.pin2, Part1.A0
  N27: J19.pin1, Part1.A3
  N28: J19.pin2, Part1.A2
  N29: J20.pin1, Part1.ioref
  N30: J20.pin2, Part1.N/C
  N31: J21.pin1, Part1.3V3
  N32: J21.pin2, Part1.RESET
  N33: Part1.VIN, J23.pin1
  N34: R6.Pin_0, LED1.anode
